# Fritzing sketch anpan_melody2_circuit_diagram (saved by Fritzing 0.9.3b)
breadboards: 1

parts:
  Speaker = Piezo Speaker
  S1 = Square Pushbutton
  waves_Arduino_Pro_Mini_互換ボード_328_5V_16MHz = Arduino Pro Mini v13
  V1 = DC Power [voltage=5]
  7_Segment1 = 7 Segment Display
  R1 = Resistor [tolerance=±5% resistance=150 package=THT]
  R2 = Resistor [tolerance=±5% resistance=150 package=THT]
  R3 = Resistor [tolerance=±5% resistance=150 package=THT]
  R4 = Resistor [tolerance=±5% resistance=150 package=THT]
  R5 = Resistor [tolerance=±5% resistance=150 package=THT]
  R6 = Resistor [tolerance=±5% resistance=150 package=THT]
  R7 = Resistor [tolerance=±5% resistance=150 package=THT]
  R8 = Resistor [tolerance=±5% resistance=150 package=THT]
  R9 = Trimmer Potentiometer [maximum_resistance=10kΩ package=THT]

nets:
  N1: Speaker.pin1, waves_Arduino_Pro_Mini_互換ボード_328_5V_16MHz.D2
  N2: Speaker.pin2, waves_Arduino_Pro_Mini_互換ボード_328_5V_16MHz.GND, V1.V-, 7_Segment1.common_cathode#8, R9.leg2
  N3: S1.leg0, V1.V+
  N4: S1.leg1, waves_Arduino_Pro_Mini_互換ボード_328_5V_16MHz.RAW
  N5: waves_Arduino_Pro_Mini_互換ボード_328_5V_16MHz.VCC, R9.leg1
  N6: waves_Arduino_Pro_Mini_互換ボード_328_5V_16MHz.A0, R9.wiper
  N7: waves_Arduino_Pro_Mini_互換ボード_328_5V_16MHz.D12/MISO, R8.Pin_1
  N8: waves_Arduino_Pro_Mini_互換ボード_328_5V_16MHz.D11_PWM/MOSI, R7.Pin_1
  N9: waves_Arduino_Pro_Mini_互換ボード_328_5V_16MHz.D10_PWM/SS, R6.Pin_1
  N10: waves_Arduino_Pro_Mini_互換ボード_328_5V_16MHz.D9_PWM, R5.Pin_1
  N11: waves_Arduino_Pro_Mini_互換ボード_328_5V_16MHz.D7, R4.Pin_1
  N12: waves_Arduino_Pro_Mini_互換ボード_328_5V_16MHz.D6_PWM, R3.Pin_1
  N13: waves_Arduino_Pro_Mini_互換ボード_328_5V_16MHz.D5_PWM, R2.Pin_1
  N14: waves_Arduino_Pro_Mini_互換ボード_328_5V_16MHz.D4, R1.Pin_1
  N15: 7_Segment1.Segment_A#1, R6.Pin_0
  N16: 7_Segment1.Segment_F, R5.Pin_0
  N17: 7_Segment1.Segment_E, R7.Pin_0
  N18: 7_Segment1.Segment_D, R8.Pin_0
  N19: 7_Segment1.Segment_DP, R2.Pin_0
  N20: 7_Segment1.Segment_C, R1.Pin_0
  N21: 7_Segment1.Segment_B, R3.Pin_0
  N22: 7_Segment1.Segment_A#10, R4.Pin_0
