# Fritzing sketch autosanitizer2 (saved by Fritzing 0.9.3b)
breadboards: 1

parts:
  J1 = Basic Servo
  VCC1 = 4 x AAA Battery Mount
  S1 = SWITCH-MOMENTARY-2 [package=tactile-pth]
  S2 = SWITCH-MOMENTARY-2 [package=tactile-pth]
  R1 = PHOTOCELL [package=photocell]
  R2 = Resistor [tolerance=±5% resistance=82k package=THT]
  LCD1 = LCD screen
  R3 = Rotary Potentiometer (Small) [maximum_resistance=10kΩ package=THT]
  Arduino_pro_mini = Arduino Pro Mini v13
  R4 = Resistor [tolerance=±5% resistance=4.7k package=THT]
  R5 = Resistor [tolerance=±5% resistance=150 package=THT]

nets:
  GND: J1.gnd, VCC1.-, S1.2, S2.2, R1.P$1, LCD1.VSS, LCD1.R/W, LCD1.LED-, R3.leg1, Arduino_pro_mini.GND
  N1: J1.vcc, VCC1.+, Arduino_pro_mini.RAW
  N2: J1.pulse, Arduino_pro_mini.D9_PWM
  N3: S1.1, Arduino_pro_mini.D3_PWM
  N4: S2.1, Arduino_pro_mini.D2
  N5: R1.P$2, R2.Pin_1, Arduino_pro_mini.A0
  VDD: R2.Pin_0, LCD1.VDD, R3.leg2, Arduino_pro_mini.VCC, R4.Pin_1, R5.Pin_1
  N6: LCD1.V0, R4.Pin_0
  N7: LCD1.RS, Arduino_pro_mini.D4
  N8: LCD1.E, Arduino_pro_mini.D6_PWM
  N9: LCD1.DB4, Arduino_pro_mini.D10_PWM/SS
  N10: LCD1.DB5, Arduino_pro_mini.D11_PWM/MOSI
  N11: LCD1.DB6, Arduino_pro_mini.D12/MISO
  N12: LCD1.DB7, Arduino_pro_mini.D13/SCK
  N13: LCD1.LED+, R5.Pin_0
  N14: R3.wiper, Arduino_pro_mini.A1
