# Fritzing sketch fiftyeight (saved by Fritzing 0.9.3b)
breadboards: 1

parts:
  ArduinoPromini = Arduino Pro Mini v13
  M8058S = IC, DIP package, 8 pins [chip_label=M8058S]
  7_Segment1 = 7 Segment Display
  7_Segment2 = 7 Segment Display
  S1 = SWITCH-MOMENTARY-2 [package=tactile_switch_tall]
  S2 = SWITCH-MOMENTARY-2 [package=tactile_switch_tall]
  2SC1815_NPN = TRANSISTOR_NPN [package=to-92]
  U1 = 74HC595 [package="DIP16 [THT]"]
  R1 = Rotary Potentiometer (Small) [maximum_resistance=100kΩ package=THT]
  VCC1 = Battery
  R2 = Resistor [tolerance=±5% resistance=2.2k package=THT]
  R3 = Resistor [tolerance=±5% resistance=1k package=THT]
  R4 = Resistor [tolerance=±5% resistance=150 package=THT]
  R5 = Resistor [tolerance=±5% resistance=2.2k package=THT]
  SP1 = SPEAKER [package=pcb_mount_speaker]
  R6 = Resistor [tolerance=±5% resistance=100k package=THT]
  R7 = Resistor [tolerance=±5% resistance=1k package=THT]
  R8 = Resistor [tolerance=±5% resistance=150 package=THT]
  R9 = Resistor [tolerance=±5% resistance=150 package=THT]
  R10 = Resistor [tolerance=±5% resistance=150 package=THT]
  R11 = Resistor [tolerance=±5% resistance=150 package=THT]
  R12 = Resistor [tolerance=±5% resistance=150 package=THT]
  R13 = Resistor [tolerance=±5% resistance=150 package=THT]
  R14 = Resistor [tolerance=±5% resistance=150 package=THT]
  R15 = Resistor [tolerance=±5% resistance=150 package=THT]
  C1 = Electrolytic Capacitor [capacitance=10μF package="0605 [SMD, electrolytic]"]

nets:
  VCC: ArduinoPromini.VCC, U1.MR, U1.VCC, R5.Pin_0, R7.Pin_1
  GND: ArduinoPromini.GND, M8058S.pin4, S1.2, S2.2, 2SC1815_NPN.E, U1.GND, U1.OE, VCC1.-, R2.Pin_1, C1.-
  N1: ArduinoPromini.RAW, M8058S.pin3, VCC1.+, C1.+
  N2: ArduinoPromini.A0, R1.wiper, R1.leg2, R3.Pin_0, R4.Pin_0, R5.Pin_1
  N3: ArduinoPromini.D5_PWM, U1.DS
  N4: ArduinoPromini.D4, U1.SH_CP
  N5: ArduinoPromini.D3_PWM, U1.ST_CP
  N6: ArduinoPromini.D2, M8058S.pin7
  N7: M8058S.pin1, SP1.+
  N8: M8058S.pin2, SP1.-
  N9: M8058S.pin8, R15.Pin_1
  N10: 7_Segment1.Segment_E, 7_Segment2.Segment_E, R12.Pin_0
  N11: 7_Segment1.Segment_D, 7_Segment2.Segment_D, R11.Pin_0
  N12: 7_Segment1.common_anode, U1.Q7, R6.Pin_1
  N13: 7_Segment1.Segment_C, 7_Segment2.Segment_C, R10.Pin_0
  N14: 7_Segment1.Segment_DP, 7_Segment2.Segment_DP, R15.Pin_0
  N15: 7_Segment1.Segment_B, 7_Segment2.Segment_B, R9.Pin_0
  N16: 7_Segment1.Segment_A, 7_Segment2.Segment_A, R8.Pin_0
  N17: 7_Segment1.Segment_F, 7_Segment2.Segment_F, R13.Pin_0
  N18: 7_Segment1.Segment_G, 7_Segment2.Segment_G, R14.Pin_0
  N19: 7_Segment2.common_anode, 2SC1815_NPN.C, R7.Pin_0
  N20: S1.1, R4.Pin_1
  N21: S2.1, R3.Pin_1
  N22: 2SC1815_NPN.B, R6.Pin_0
  N23: U1.Q1, R9.Pin_1
  N24: U1.Q2, R10.Pin_1
  N25: U1.Q3, R11.Pin_1
  N26: U1.Q4, R12.Pin_1
  N27: U1.Q5, R13.Pin_1
  N28: U1.Q6, R14.Pin_1
  N29: U1.Q0, R8.Pin_1
  N30: R1.leg1, R2.Pin_0
