# Fritzing sketch levelupbox_circuit_diagram (saved by Fritzing 0.9.3b)
breadboards: 1

parts:
  Speaker = Piezo Speaker
  S1 = Square Pushbutton
  waves_Arduino_Pro_Mini_互換ボード_328_5V_16MHz = Arduino Pro Mini v13
  V1 = DC Power [voltage=5]
  LED1 = LED - 5mm [color="Blue (525nm)" package="5 mm [THT]"]
  R1 = Resistor [tolerance=±5% resistance=150 package=THT]
  S2 = SWITCH-MOMENTARY-2 [package=tactile-pth-12mm]

nets:
  N1: Speaker.pin1, waves_Arduino_Pro_Mini_互換ボード_328_5V_16MHz.D2
  N2: Speaker.pin2, waves_Arduino_Pro_Mini_互換ボード_328_5V_16MHz.GND, V1.V-, LED1.cathode, S2.1
  N3: S1.leg0, V1.V+
  N4: S1.leg1, waves_Arduino_Pro_Mini_互換ボード_328_5V_16MHz.RAW
  N5: waves_Arduino_Pro_Mini_互換ボード_328_5V_16MHz.D10_PWM/SS, S2.2
  N6: waves_Arduino_Pro_Mini_互換ボード_328_5V_16MHz.D8, R1.Pin_1
  N7: LED1.anode, R1.Pin_0
