# Fritzing sketch melody_gift_box (saved by Fritzing 0.9.3b)
breadboards: 1

parts:
  2N3906 = PNP-Transistor [package="TO92 [THT]"]
  SP1 = SPEAKER [package=pcb_mount_speaker]
  BATT1 = FKIT-COIN_CELL [package=fkit-lir2450-h]
  UM66T08LU = mystery part, 3 pins [chip_label="Melody IC"]
  LED1 = LED - 5mm [color="Blue (525nm)" package="5 mm [THT]"]
  R1 = Resistor [tolerance=±5% resistance=4.7k package=THT]
  GL5537_2MΩ = PHOTOCELL [package=photocell-kit]
  R3 = Resistor [tolerance=±5% resistance=150 package=THT]  # not connected

nets (from the schematic view):
  N1: 2N3906.E, BATT1.POS, R1.Pin_0
  N2: 2N3906.B, R1.Pin_1, GL5537_2MΩ.P$1
  N3: 2N3906.C, UM66T08LU.pin1
  N4: SP1.+, UM66T08LU.pin3
  N5: SP1.-, BATT1.NEG, UM66T08LU.pin2, LED1.cathode, GL5537_2MΩ.P$2
