# Fritzing sketch test_for_sg92r (saved by Fritzing 0.9.3b)
breadboards: 1

parts:
  パーツ1 = Arduino Pro Mini (5V)
  J1 = Basic Servo
  VCC1 = 4 x AAA Battery Mount
  S1 = SWITCH-MOMENTARY-2 [package=tactile-pth]
  S2 = SWITCH-MOMENTARY-2 [package=tactile-pth]
  S3 = SWITCH-MOMENTARY-2 [package=tactile-pth]
  R1 = PHOTOCELL [package=photocell]
  R2 = Resistor [tolerance=±5% resistance=82k package=THT]

nets:
  VCC: パーツ1.VCC, J1.vcc, R2.Pin_0
  N1: パーツ1.RAW, VCC1.+
  GND: パーツ1.GND, J1.gnd, VCC1.-, S1.1, S2.1, S3.1, R1.P$1
  N2: パーツ1.A0, R1.P$2, R2.Pin_1
  N3: パーツ1.D9, J1.pulse
  N4: パーツ1.D4, S3.2
  N5: パーツ1.D3, S2.2
  N6: パーツ1.D2, S1.2
