# Fritzing sketch water_the_plants (saved by Fritzing 0.9.3b)
breadboards: 1

parts:
  U1 = RELAY [package=OJ]
  パーツ1 = Arduino Pro Mini v13
  パーツ2 = Lilypad Power Supply
  M1 = DC Motor
  U2 = SWITCH-SPST-2 [package=switch-spst-vertical]
  R1 = Resistor [tolerance=±5% resistance=150 package=THT]
  LED1 = LED - 5mm [color="Green (570nm)" package="5 mm [THT]"]
  S1 = Pushbutton [package="[SMD]"]

nets (from the schematic view):
  GND: U1.COIL2, パーツ1.GND, パーツ2.GND, LED1.cathode, S1.Pin_3
  N1: U1.MAIN, M1.pin_2
  N2: U1.NO, M1.pin_1
  N3: U1.COIL1, パーツ1.D2
  N4: パーツ1.RAW, U2.O
  N5: パーツ1.D4, S1.Pin_1, S1.Pin_2
  N6: パーツ1.D3_PWM, R1.Pin_1
  N7: パーツ2.+, U2.P
  N8: R1.Pin_0, LED1.anode
